# Fritzing sketch Dimmer_12v (saved by Fritzing 0.9.5d)

parts:
  Part1 = Arduino Nano (Rev3.0)
  Q1 = Basic FET P-Channel [package="TO220 [THT]"]
  R2 = Resistor [tolerance=±5% resistance=10k package=THT]  # not connected
  R1 = Resistor [tolerance=±5% resistance=100 package=THT]
  U2 = POT [package=trim_pot]  # not connected
  U3 = POT_SWITCH [package=pot_pth]  # not connected
  U4 = POT [part_number=10k package=pot_mammoth]

nets:
  N1: Part1.D5, R1.Pin_0
  N2: Part1.5V, U4.E
  N3: Part1.A0, U4.A
  N4: Q1.gate, R1.Pin_1

notes:
  LED (12v)
  Power supply (12v)
